# Fritzing sketch flagday (saved by Fritzing 1.0.6)
breadboards: 1

parts:
  Mod1 = Heltec WiFi LoRa 32 V3 [part_number=HTIT-WB32LA]
  RE1 = Rotary Encoder [package=THT]
  A1 = MH-FMD buzzer

nets:
  N1: Mod1.pin_4, Mod1.pin_26
  N2: Mod1.pin_7, Mod1.pin_9, Mod1.pin_13, A1.Pin_1
  N3: Mod1.pin_8, RE1.EncoderPinB
  N4: Mod1.pin_22, Mod1.pin_30
  N5: RE1.EncoderPinC, RE1.SwitchrPinD, A1.Pin_3

custom parts:
  Heltec WiFi LoRa 32 V3: The Heltec WiFi LoRa 32 is an IoT development board designed and produced by Heltec Automation and based on the Espressif ESP32-S3FN8 and Semtech SX1262 modules. The board includes WiFi, Bluetooth and LoRa functions, as well as a 0.96″ OLED display and a lithium battery management system. Links: Heltec WiFi LoRa 32 product page Github
  Rotary Encoder: Rotary Encoder from ALPSec11e with switch.
  MH-FMD buzzer: MH-FMD buzzer.
